// Logisim project CPU.circ as structural Verilog
module OR008 (
  input  in_1,
  input  in_2,
  input  in_3,
  input  in_4,
  input  in_5,
  input  in_6,
  input  in_7,
  input  in_8,
  input  in_9,
  input  in_10,
  input  in_11,
  input  in_12,
  input  in_13,
  input  in_14,
  input  in_15,
  input  in_16,
  output O7,
  output O6,
  output O5,
  output O4,
  output O3,
  output O2,
  output O1,
  output O0
);

  or or_1 (O7, in_1, in_3);
  or or_2 (O5, in_4, in_7);
  or or_3 (O6, in_2, in_5, in_5);
  or or_4 (O4, in_6, in_9);
  or or_5 (O3, in_8, in_11);
  or or_6 (O2, in_10, in_13);
  or or_7 (O0, in_14, in_16);
  or or_8 (O1, in_12, in_15);
endmodule

module AND008 (
  input  in_1,
  input  in_2,
  input  in_3,
  input  in_4,
  input  in_5,
  input  in_6,
  input  in_7,
  input  in_8,
  input  in_9,
  input  in_10,
  input  in_11,
  input  in_12,
  input  in_13,
  input  in_14,
  input  in_15,
  input  in_16,
  output out_17,
  output out_18,
  output out_19,
  output out_20,
  output out_21,
  output out_22,
  output out_23,
  output out_24
);

  xor xor_1 (out_17, in_1, in_3);
  xor xor_2 (out_18, in_2, in_5);
  xor xor_3 (out_19, in_4, in_7);
  xor xor_4 (out_20, in_6, in_9);
  xor xor_5 (out_22, in_10, in_13);
  xor xor_6 (out_21, in_8, in_11);
  xor xor_7 (out_23, in_12, in_15);
  xor xor_8 (out_24, in_14, in_16);
endmodule

module XOR008 (
  input  in_1,
  input  in_2,
  input  in_3,
  input  in_4,
  input  in_5,
  input  in_6,
  input  in_7,
  input  in_8,
  input  in_9,
  input  in_10,
  input  in_11,
  input  in_12,
  input  in_13,
  input  in_14,
  input  in_15,
  input  in_16,
  output out_17,
  output out_18,
  output out_19,
  output out_20,
  output out_21,
  output out_22,
  output out_23,
  output out_24
);

  xor xor_1 (out_17, in_1, in_3);
  xor xor_2 (out_18, in_2, in_5);
  xor xor_3 (out_20, in_6, in_9);
  xor xor_4 (out_19, in_4, in_7);
  xor xor_5 (out_21, in_8, in_11);
  xor xor_6 (out_22, in_10, in_13);
  xor xor_7 (out_23, in_12, in_15);
  xor xor_8 (out_24, in_14, in_16);
endmodule

module NOT008 (
  input  in_1,
  input  in_2,
  input  in_3,
  input  in_4,
  input  in_5,
  input  in_6,
  input  in_7,
  input  in_8,
  input  in_9,
  output out_10,
  output out_11,
  output out_12,
  output out_13,
  output out_14,
  output out_15,
  output out_16,
  output out_17
);

  wire not_1_out, not_2_out, not_3_out, not_4_out, not_5_out, not_6_out, not_7_out, not_8_out;

  not not_1 (not_1_out, in_1);
  not not_2 (not_2_out, in_2);
  not not_3 (not_3_out, in_3);
  not not_4 (not_4_out, in_4);
  not not_5 (not_5_out, in_5);
  not not_6 (not_6_out, in_6);
  not not_7 (not_7_out, in_7);
  not not_8 (not_8_out, in_8);
  and and_1 (out_10, not_1_out, in_9);
  and and_2 (out_11, not_2_out, in_9);
  and and_3 (out_12, not_3_out, in_9);
  and and_4 (out_13, not_4_out, in_9);
  and and_5 (out_14, not_5_out, in_9);
  and and_6 (out_15, not_6_out, in_9);
  and and_7 (out_16, not_7_out, in_9);
  and and_8 (out_17, not_8_out, in_9);
endmodule

module FullAdder (
  input  in_1,
  input  in_2,
  input  in_3,
  output S,
  output R
);

  wire and_1_out, and_2_out, xor_1_out;

  xor xor_1 (xor_1_out, in_1, in_2);
  and and_1 (and_1_out, in_1, in_2);
  xor xor_2 (S, xor_1_out, in_3);
  and and_2 (and_2_out, xor_1_out, in_3);
  or or_1 (R, and_1_out, and_2_out);
endmodule

module ADD008 (
  input  A7,
  input  B7,
  input  A6,
  input  B6,
  input  A5,
  input  B5,
  input  A4,
  input  B4,
  input  A3,
  input  B3,
  input  A2,
  input  B2,
  input  A1,
  input  B1,
  input  A0,
  input  B0,
  output C,
  output S7,
  output S6,
  output S5,
  output s4,
  output S3,
  output S2,
  output S1,
  output S0
);

  wire fulladder_1_r, fulladder_3_r, fulladder_4_r, fulladder_5_r, fulladder_6_r, fulladder_7_r,
       fulladder_8_r;

  FullAdder fulladder_1 (.in_1(B6), .in_2(A6), .in_3(fulladder_4_r), .S(S6), .R(fulladder_1_r));
  FullAdder fulladder_2 (.in_1(B7), .in_2(A7), .in_3(fulladder_1_r), .S(S7), .R(C));
  FullAdder fulladder_3 (.in_1(B4), .in_2(A4), .in_3(fulladder_6_r), .S(s4), .R(fulladder_3_r));
  FullAdder fulladder_4 (.in_1(B5), .in_2(A5), .in_3(fulladder_3_r), .S(S5), .R(fulladder_4_r));
  FullAdder fulladder_5 (.in_1(B2), .in_2(A2), .in_3(fulladder_8_r), .S(S2), .R(fulladder_5_r));
  FullAdder fulladder_6 (.in_1(B3), .in_2(A3), .in_3(fulladder_5_r), .S(S3), .R(fulladder_6_r));
  FullAdder fulladder_7 (.in_1(B0), .in_2(A0), .in_3(1'b0), .S(S0), .R(fulladder_7_r));
  FullAdder fulladder_8 (.in_1(B1), .in_2(A1), .in_3(fulladder_7_r), .S(S1), .R(fulladder_8_r));
endmodule

module AND_Selective (
  input  A7,
  input  A6,
  input  A5,
  input  A4,
  input  A3,
  input  A2,
  input  A1,
  input  A0,
  input  B7,
  input  B6,
  input  B5,
  input  B4,
  input  B3,
  input  B2,
  input  B1,
  input  B0,
  input  Signal_D,
  output out_18,
  output out_19,
  output out_20,
  output out_21,
  output out_22,
  output out_23,
  output out_24,
  output out_25,
  output out_26,
  output out_27,
  output out_28,
  output out_29,
  output out_30,
  output out_31,
  output out_32,
  output out_33
);

  and and_1 (out_18, A7, Signal_D);
  and and_2 (out_19, A6, Signal_D);
  and and_3 (out_20, A5, Signal_D);
  and and_4 (out_21, A4, A4, Signal_D);
  and and_5 (out_22, A3, Signal_D);
  and and_6 (out_23, A2, Signal_D);
  and and_7 (out_24, A1, Signal_D);
  and and_8 (out_25, A0, Signal_D);
  and and_9 (out_26, B7, Signal_D, Signal_D);
  and and_10 (out_27, B6, Signal_D);
  and and_11 (out_28, B5, Signal_D);
  and and_12 (out_29, Signal_D, Signal_D, B4);
  and and_13 (out_30, B3, Signal_D);
  and and_14 (out_31, B2, Signal_D);
  and and_15 (out_32, B1, Signal_D);
  and and_16 (out_33, B0, Signal_D);
endmodule

module DECODEUR_3Bit (
  input  e1,
  input  e2,
  input  e3,
  output s0,
  output s1,
  output s2,
  output s3,
  output s4,
  output s5,
  output s7
);

  wire not_1_out, not_2_out, not_3_out, not_4_out, not_5_out, not_6_out;

  not not_1 (not_1_out, e1);
  not not_2 (not_2_out, e2);
  not not_3 (not_3_out, e3);
  not not_4 (not_4_out, e1);
  not not_5 (not_5_out, e1);
  and and_1 (s0, not_1_out, not_2_out, not_3_out, not_3_out);
  and and_2 (s1, e1, not_2_out, not_3_out);
  and and_3 (s2, not_3_out, e2, not_4_out);
  and and_4 (s3, e1, e2, not_3_out);
  not not_6 (not_6_out, e2);
  and and_5 (s4, not_5_out, not_6_out, e3);
  and and_6 (s5, e3, e1, not_6_out);
  and and_7 (s7, not_5_out, e2, e3);
endmodule

module OverFlow (
  input  A,
  input  B,
  input  S,
  output out_4
);

  wire xor_1_out, xor_2_out;

  xor xor_1 (xor_1_out, A, S);
  xor xor_2 (xor_2_out, S, B);
  and and_1 (out_4, xor_1_out, xor_2_out);
endmodule

module Zero (
  input  in_1,
  input  in_2,
  input  in_3,
  input  in_4,
  input  in_5,
  input  in_6,
  input  in_7,
  input  in_8,
  output out_9
);

  wire and_1_out, and_2_out, not008_1_out_10, not008_1_out_11, not008_1_out_12, not008_1_out_13,
       not008_1_out_14, not008_1_out_15, not008_1_out_16, not008_1_out_17;

  NOT008 not008_1 (
    .in_1(in_1), .in_2(in_2), .in_3(in_3), .in_4(in_4), .in_5(in_5), .in_6(in_6), .in_7(in_7), .in_8(in_8),
    .in_9(1'b1), .out_10(not008_1_out_10), .out_11(not008_1_out_11), .out_12(not008_1_out_12),
    .out_13(not008_1_out_13), .out_14(not008_1_out_14), .out_15(not008_1_out_15), .out_16(not008_1_out_16),
    .out_17(not008_1_out_17));
  and and_1 (and_1_out, not008_1_out_10, not008_1_out_11, not008_1_out_12, not008_1_out_13);
  and and_2 (and_2_out, not008_1_out_14, not008_1_out_15, not008_1_out_16, not008_1_out_17);
  and and_3 (out_9, and_1_out, and_2_out);
endmodule

module SHR (
  input  A7,
  input  in_2,
  input  in_3,
  input  in_4,
  input  in_5,
  input  in_6,
  input  A0,
  input  in_8,
  input  dec_com,
  output C,
  output S7,
  output out_12,
  output out_13,
  output out_14,
  output out_15,
  output out_16,
  output S0,
  output out_18
);

  and and_1 (out_12, dec_com, A7);
  and and_2 (out_13, dec_com, in_2);
  and and_3 (out_14, dec_com, in_3);
  and and_4 (out_15, dec_com, in_4);
  and and_5 (out_16, dec_com, in_5);
  and and_6 (S0, dec_com, in_6, in_6);
  and and_7 (out_18, dec_com, A0);
  and and_8 (C, dec_com, in_8);

  assign S7 = 1'b0;
endmodule

module SHL (
  input  A7,
  input  in_2,
  input  in_3,
  input  in_4,
  input  in_5,
  input  in_6,
  input  A0,
  input  in_8,
  input  dec_com,
  output C,
  output S7,
  output out_12,
  output out_13,
  output out_14,
  output out_15,
  output out_16,
  output S0,
  output out_18
);

  and and_1 (C, dec_com, A7);
  and and_2 (S7, dec_com, in_2);
  and and_3 (out_12, dec_com, in_3);
  and and_4 (out_13, dec_com, in_4);
  and and_5 (out_14, dec_com, in_5);
  and and_6 (out_15, dec_com, in_6, in_6);
  and and_7 (out_16, dec_com, A0);
  and and_8 (S0, dec_com, in_8);

  assign out_18 = 1'b0;
endmodule

module Flip_Flop_D_8bit (
  input  in_1,
  input  in_2,
  input  in_3,
  input  in_4,
  input  in_5,
  input  in_6,
  input  in_7,
  input  in_8,
  input  H,
  input  S,
  input  R,
  output out_12,
  output out_13,
  output out_14,
  output out_15,
  output out_16,
  output out_17,
  output out_18,
  output out_19
);

  D_Flip_Flop d_ff_1 (.clk(H), .D(in_1), .Q(out_12), .preset(R), .en(S), .reset(1'b0));  // open: Qn
  D_Flip_Flop d_ff_2 (.clk(H), .D(in_2), .Q(out_13), .preset(R), .en(S), .reset(1'b0));  // open: Qn
  D_Flip_Flop d_ff_3 (.clk(H), .D(in_3), .Q(out_14), .preset(R), .en(S), .reset(1'b0));  // open: Qn
  D_Flip_Flop d_ff_4 (.clk(H), .D(in_4), .Q(out_15), .preset(R), .en(S), .reset(1'b0));  // open: Qn
  D_Flip_Flop d_ff_5 (.clk(H), .D(in_5), .Q(out_16), .preset(R), .en(S), .reset(1'b0));  // open: Qn
  D_Flip_Flop d_ff_6 (.clk(H), .D(in_6), .Q(out_17), .preset(R), .en(S), .reset(1'b0));  // open: Qn
  D_Flip_Flop d_ff_7 (.clk(H), .D(in_7), .Q(out_18), .preset(R), .en(S), .reset(1'b0));  // open: Qn
  D_Flip_Flop d_ff_8 (.clk(H), .D(in_8), .Q(out_19), .preset(R), .en(S), .reset(1'b0));  // open: Qn
endmodule

module DECODEUR_2Bit (
  input  E0,
  input  E1,
  output out_3,
  output out_4,
  output out_5,
  output out_6
);

  wire not_1_out, not_2_out;

  not not_1 (not_1_out, E0);
  not not_2 (not_2_out, E1);
  and and_1 (out_3, not_1_out, not_2_out);
  and and_2 (out_4, not_2_out, E0);
  and and_3 (out_5, E1, not_1_out);
  and and_4 (out_6, E1, E0);
endmodule

module Flip_Flop_D_4bit (
  input  in_1,
  input  in_2,
  input  in_3,
  input  in_4,
  input  H,
  input  S,
  input  R,
  output out_8,
  output out_9,
  output out_10,
  output out_11
);

  D_Flip_Flop d_ff_1 (.clk(H), .D(in_1), .Q(out_8), .preset(R), .en(S), .reset(1'b0));  // open: Qn
  D_Flip_Flop d_ff_2 (.clk(H), .D(in_2), .Q(out_9), .preset(R), .en(S), .reset(1'b0));  // open: Qn
  D_Flip_Flop d_ff_3 (.clk(H), .D(in_3), .Q(out_10), .preset(R), .en(S), .reset(1'b0));  // open: Qn
  D_Flip_Flop d_ff_4 (.clk(H), .D(in_4), .Q(out_11), .preset(R), .en(S), .reset(1'b0));  // open: Qn
endmodule

module PC_ADD (
  input  in_1,
  input  in_2,
  input  in_3,
  input  in_4,
  input  in_5,
  input  in_6,
  input  in_7,
  input  in_8,
  output out_9,
  output out_10,
  output out_11,
  output out_12,
  output out_13,
  output out_14,
  output out_15,
  output out_16
);

  wire halfadder_2_r_2, halfadder_3_r_2, halfadder_4_r_2, halfadder_5_r_2, halfadder_6_r_2, halfadder_7_r_2,
       halfadder_8_r_2;

  HalfAdder halfadder_1 (.A(in_1), .R(halfadder_3_r_2), .S(out_9));  // open: R_2
  HalfAdder halfadder_2 (.A(in_3), .R(halfadder_4_r_2), .S(out_11), .R_2(halfadder_2_r_2));
  HalfAdder halfadder_3 (.A(in_2), .R(halfadder_2_r_2), .S(out_10), .R_2(halfadder_3_r_2));
  HalfAdder halfadder_4 (.A(in_4), .R(halfadder_5_r_2), .S(out_12), .R_2(halfadder_4_r_2));
  HalfAdder halfadder_5 (.A(in_5), .R(halfadder_6_r_2), .S(out_13), .R_2(halfadder_5_r_2));
  HalfAdder halfadder_6 (.A(in_6), .R(halfadder_8_r_2), .S(out_14), .R_2(halfadder_6_r_2));
  HalfAdder halfadder_7 (.A(in_8), .R(1'b1), .S(out_16), .R_2(halfadder_7_r_2));
  HalfAdder halfadder_8 (.A(in_7), .R(halfadder_7_r_2), .S(out_15), .R_2(halfadder_8_r_2));
endmodule

module HalfAdder (
  input  A,
  input  R,
  output S,
  output R_2
);

  wire and_1_out, and_2_out, not_1_out, not_2_out;

  not not_1 (not_1_out, A);
  not not_2 (not_2_out, R);
  and and_1 (and_1_out, not_1_out, R);
  and and_2 (and_2_out, not_2_out, A);
  and and_3 (R_2, A, R);
  or or_1 (S, and_1_out, and_2_out);
endmodule

module MUL_PC (
  input  in_1,
  input  in_2,
  input  in_3,
  input  PC_1,
  input  in_5,
  input  in_6,
  input  in_7,
  input  in_8,
  input  in_9,
  input  in_10,
  input  JUMP,
  input  in_12,
  input  in_13,
  input  in_14,
  input  in_15,
  input  in_16,
  input  in_17,
  output out_18,
  output out_19,
  output out_20,
  output out_21,
  output out_22,
  output out_23,
  output out_24,
  output out_25
);

  wire and_2bit_1_out_3, and_2bit_2_out_3, and_2bit_3_out_3, and_2bit_4_out_3, and_2bit_5_out_3,
       and_2bit_6_out_3, and_2bit_7_out_3, and_2bit_8_out_3, and_2bit_9_out_3, and_2bit_10_out_3,
       and_2bit_11_out_3, and_2bit_12_out_3, and_2bit_13_out_3, and_2bit_14_out_3, and_2bit_15_out_3,
       and_2bit_16_out_3, not_1_out;

  AND_2bit and_2bit_1 (.in_1(in_1), .in_2(not_1_out), .out_3(and_2bit_1_out_3));
  AND_2bit and_2bit_2 (.in_1(in_2), .in_2(not_1_out), .out_3(and_2bit_2_out_3));
  AND_2bit and_2bit_3 (.in_1(in_3), .in_2(not_1_out), .out_3(and_2bit_3_out_3));
  AND_2bit and_2bit_4 (.in_1(PC_1), .in_2(not_1_out), .out_3(and_2bit_4_out_3));
  AND_2bit and_2bit_5 (.in_1(in_5), .in_2(not_1_out), .out_3(and_2bit_5_out_3));
  AND_2bit and_2bit_6 (.in_1(in_6), .in_2(not_1_out), .out_3(and_2bit_6_out_3));
  AND_2bit and_2bit_7 (.in_1(in_7), .in_2(not_1_out), .out_3(and_2bit_7_out_3));
  AND_2bit and_2bit_8 (.in_1(in_8), .in_2(not_1_out), .out_3(and_2bit_8_out_3));
  not not_1 (not_1_out, in_17);
  AND_2bit and_2bit_9 (.in_1(in_9), .in_2(in_17), .out_3(and_2bit_9_out_3));
  AND_2bit and_2bit_10 (.in_1(in_10), .in_2(in_17), .out_3(and_2bit_10_out_3));
  AND_2bit and_2bit_11 (.in_1(JUMP), .in_2(in_17), .out_3(and_2bit_11_out_3));
  AND_2bit and_2bit_12 (.in_1(in_12), .in_2(in_17), .out_3(and_2bit_12_out_3));
  AND_2bit and_2bit_13 (.in_1(in_13), .in_2(in_17), .out_3(and_2bit_13_out_3));
  AND_2bit and_2bit_14 (.in_1(in_14), .in_2(in_17), .out_3(and_2bit_14_out_3));
  AND_2bit and_2bit_15 (.in_1(in_15), .in_2(in_17), .out_3(and_2bit_15_out_3));
  AND_2bit and_2bit_16 (.in_1(in_16), .in_2(in_17), .out_3(and_2bit_16_out_3));
  or or_1 (out_18, and_2bit_1_out_3, and_2bit_9_out_3);
  or or_2 (out_19, and_2bit_2_out_3, and_2bit_10_out_3);
  or or_3 (out_20, and_2bit_3_out_3, and_2bit_11_out_3);
  or or_4 (out_21, and_2bit_4_out_3, and_2bit_12_out_3);
  or or_5 (out_22, and_2bit_5_out_3, and_2bit_13_out_3);
  or or_6 (out_23, and_2bit_6_out_3, and_2bit_14_out_3);
  or or_7 (out_24, and_2bit_7_out_3, and_2bit_15_out_3);
  or or_8 (out_25, and_2bit_8_out_3, and_2bit_16_out_3);
endmodule

module AND_2bit (
  input  in_1,
  input  in_2,
  output out_3
);

  and and_1 (out_3, in_1, in_2);
endmodule

module Flip_Flop_D_16bit (
  input  in_1,
  input  in_2,
  input  in_3,
  input  in_4,
  input  in_5,
  input  in_6,
  input  in_7,
  input  in_8,
  input  in_9,
  input  in_10,
  input  in_11,
  input  in_12,
  input  in_13,
  input  in_14,
  input  in_15,
  input  in_16,
  input  H,
  input  S,
  input  R,
  output out_20,
  output out_21,
  output out_22,
  output out_23,
  output out_24,
  output out_25,
  output out_26,
  output out_27,
  output out_28,
  output out_29,
  output out_30,
  output out_31,
  output out_32,
  output out_33,
  output out_34,
  output out_35
);

  Flip_Flop_D_8bit flip_flop_d_8bit_1 (
    .H(H), .S(S), .R(R), .in_1(in_1), .in_2(in_2), .in_3(in_3), .in_4(in_4), .in_5(in_5), .in_6(in_6),
    .in_7(in_7), .in_8(in_8), .out_12(out_20), .out_13(out_21), .out_14(out_22), .out_15(out_23),
    .out_16(out_24), .out_17(out_25), .out_18(out_26), .out_19(out_27));
  Flip_Flop_D_8bit flip_flop_d_8bit_2 (
    .H(H), .S(S), .R(R), .in_1(in_9), .in_2(in_10), .in_3(in_11), .in_4(in_12), .in_5(in_13), .in_6(in_14),
    .in_7(in_15), .in_8(in_16), .out_12(out_28), .out_13(out_29), .out_14(out_30), .out_15(out_31),
    .out_16(out_32), .out_17(out_33), .out_18(out_34), .out_19(out_35));
endmodule

module TEST_RAM_4_8octets (
  input  R_W,
  input  in_2,
  input  in_3,
  input  in_4,
  input  in_5,
  input  in_6,
  input  in_7,
  input  in_8,
  input  in_9,
  input  H,
  input  R,
  input  A0,
  input  A1
);

  wire and_2bit_1_out_3, and_2bit_2_out_3, and_2bit_3_out_3, and_2bit_4_out_3, and_2bit_5_out_3,
       and_2bit_6_out_3, and_2bit_7_out_3, and_2bit_8_out_3, decodeur_2bit_1_out_3, decodeur_2bit_1_out_4,
       decodeur_2bit_1_out_5, decodeur_2bit_1_out_6;

  DECODEUR_2Bit decodeur_2bit_1 (
    .E0(A0), .E1(A1), .out_3(decodeur_2bit_1_out_3), .out_4(decodeur_2bit_1_out_4),
    .out_5(decodeur_2bit_1_out_5), .out_6(decodeur_2bit_1_out_6));
  AND_2bit and_2bit_1 (.in_1(in_2), .in_2(R_W), .out_3(and_2bit_1_out_3));
  AND_2bit and_2bit_2 (.in_1(in_3), .in_2(R_W), .out_3(and_2bit_2_out_3));
  AND_2bit and_2bit_3 (.in_1(in_5), .in_2(R_W), .out_3(and_2bit_3_out_3));
  AND_2bit and_2bit_4 (.in_1(in_4), .in_2(R_W), .out_3(and_2bit_4_out_3));
  AND_2bit and_2bit_5 (.in_1(in_7), .in_2(R_W), .out_3(and_2bit_5_out_3));
  AND_2bit and_2bit_6 (.in_1(in_6), .in_2(R_W), .out_3(and_2bit_6_out_3));
  AND_2bit and_2bit_7 (.in_1(in_8), .in_2(R_W), .out_3(and_2bit_7_out_3));
  AND_2bit and_2bit_8 (.in_1(in_9), .in_2(R_W), .out_3(and_2bit_8_out_3));
  Flip_Flop_D_8bit flip_flop_d_8bit_1 (
    .H(H), .S(decodeur_2bit_1_out_3), .R(R), .in_1(and_2bit_1_out_3), .in_2(and_2bit_2_out_3),
    .in_3(and_2bit_4_out_3), .in_4(and_2bit_3_out_3), .in_5(and_2bit_6_out_3), .in_6(and_2bit_5_out_3),
    .in_7(and_2bit_7_out_3), .in_8(and_2bit_8_out_3));  // open: out_12, out_13, out_14, out_15, out_16, out_17, out_18, out_19
  Flip_Flop_D_8bit flip_flop_d_8bit_2 (
    .H(H), .S(decodeur_2bit_1_out_4), .R(R), .in_1(and_2bit_1_out_3), .in_2(and_2bit_2_out_3),
    .in_3(and_2bit_4_out_3), .in_4(and_2bit_3_out_3), .in_5(and_2bit_6_out_3), .in_6(and_2bit_5_out_3),
    .in_7(and_2bit_7_out_3), .in_8(and_2bit_8_out_3));  // open: out_12, out_13, out_14, out_15, out_16, out_17, out_18, out_19
  Flip_Flop_D_8bit flip_flop_d_8bit_3 (
    .H(H), .S(decodeur_2bit_1_out_5), .R(R), .in_1(and_2bit_1_out_3), .in_2(and_2bit_2_out_3),
    .in_3(and_2bit_4_out_3), .in_4(and_2bit_3_out_3), .in_5(and_2bit_6_out_3), .in_6(and_2bit_5_out_3),
    .in_7(and_2bit_7_out_3), .in_8(and_2bit_8_out_3));  // open: out_12, out_13, out_14, out_15, out_16, out_17, out_18, out_19
  Flip_Flop_D_8bit flip_flop_d_8bit_4 (
    .H(H), .S(decodeur_2bit_1_out_6), .R(R), .in_1(and_2bit_1_out_3), .in_2(and_2bit_2_out_3),
    .in_3(and_2bit_4_out_3), .in_4(and_2bit_3_out_3), .in_5(and_2bit_6_out_3), .in_6(and_2bit_5_out_3),
    .in_7(and_2bit_7_out_3), .in_8(and_2bit_8_out_3));  // open: out_12, out_13, out_14, out_15, out_16, out_17, out_18, out_19
endmodule

module OPCODE_CIRCUIT (
  input  in_1,
  input  in_2,
  input  in_3,
  input  in_4,
  input  MODE_MOVE,
  input  in_6,
  input  Z,
  input  N,
  output out_9,
  output SEL_ALU,
  output out_11,
  output Stc_D,
  output JUMP,
  output stc_RAM,
  output SEL_ADDR,
  output HLT,
  output SEL_SRC,
  output out_18
);

  wire and_2_out, and_2bit_1_out_3, and_2bit_2_out_3, and_2bit_3_out_3, and_2bit_4_out_3, and_2bit_5_out_3,
       and_2bit_6_out_3, and_2bit_7_out_3, and_2bit_8_out_3, and_2bit_9_out_3, and_3_out, and_4_out,
       and_5_out, and_6_out, and_7_out, and_8_out, and_9_out, and_10_out, and_11_out, and_12_out, and_13_out,
       and_14_out, and_15_out, and_16_out, and_17_out, and_18_out, and_19_out, and_20_out, and_21_out,
       and_22_out, and_23_out, and_24_out, and_25_out, JG_out, JGE_out, JL_out, JLE_out, not_1_out,
       not_2_out, not_3_out, not_4_out, not_5_out, not_6_out, not_7_out, not_8_out, not_9_out, not_10_out,
       not_11_out, not_12_out, not_13_out, not_14_out, not_15_out, not_16_out, not_17_out, not_18_out,
       not_19_out, not_20_out, not_21_out, not_22_out, not_23_out, not_24_out, not_25_out, not_26_out,
       not_27_out, not_28_out, not_29_out, not_30_out, not_31_out, not_32_out, not_33_out, not_34_out,
       or_2bit_1_out_3, or_2bit_3_out_3, or_4_out, or_5_out, or_6_out, or_8_out;

  not not_1 (not_1_out, in_1);
  not not_2 (not_2_out, in_2);
  not not_3 (not_3_out, in_4);
  not not_4 (not_4_out, in_2);
  not not_5 (not_5_out, in_1);
  not not_6 (not_6_out, in_1);
  not not_7 (not_7_out, in_1);
  not not_8 (not_8_out, in_2);
  not not_9 (not_9_out, in_1);
  not not_10 (not_10_out, in_4);
  not not_11 (not_11_out, in_4);
  not not_12 (not_12_out, in_3);
  not not_13 (not_13_out, in_4);
  not not_14 (not_14_out, in_1);
  not not_15 (not_15_out, in_2);
  not not_16 (not_16_out, in_3);
  not not_17 (not_17_out, in_4);
  not not_18 (not_18_out, in_3);
  not not_19 (not_19_out, in_3);
  not not_20 (not_20_out, in_3);
  not not_21 (not_21_out, in_1);
  not not_22 (not_22_out, in_3);
  not not_23 (not_23_out, in_4);
  not not_24 (not_24_out, in_2);
  and and_1 (HLT, not_13_out, in_3, in_2, in_1);
  and and_2 (and_2_out, not_14_out, not_15_out, not_16_out, not_17_out);
  and and_3 (and_3_out, in_4, not_18_out, not_2_out, not_1_out);
  and and_4 (and_4_out, not_3_out, in_3, not_4_out, not_5_out);
  and and_5 (and_5_out, not_3_out, not_19_out, in_2, not_6_out);
  and and_6 (and_6_out, not_3_out, in_3, in_2, not_7_out);
  and and_7 (and_7_out, in_4, in_3, not_8_out, not_9_out);
  and and_8 (and_8_out, not_10_out, not_20_out, in_2, not_21_out);
  and and_9 (and_9_out, in_4, in_3, in_2, not_21_out);
  and and_10 (and_10_out, in_4, not_22_out, in_2, not_21_out);
  and and_11 (and_11_out, not_23_out, in_3, in_2, not_21_out);
  and and_12 (and_12_out, in_4, in_3, in_2, not_21_out);
  and and_13 (and_13_out, not_11_out, not_12_out, not_24_out, in_1);
  and and_14 (and_14_out, in_4, not_24_out, not_12_out, in_1);
  and JG (JG_out, not_11_out, not_24_out, in_1, in_3);
  and JGE (JGE_out, in_4, in_3, in_1, not_24_out);
  and JL (JL_out, in_1, in_2, not_12_out, not_11_out);
  and JLE (JLE_out, in_4, in_2, in_1, not_12_out);
  or or_1 (out_11, and_4_out, and_5_out, and_6_out);
  or or_2 (SEL_ALU, and_7_out, and_8_out, and_9_out);
  or or_3 (out_9, and_10_out, and_11_out, and_12_out);
  OR_2Bit or_2bit_1 (.in_1(in_6), .in_2(not_25_out), .out_3(or_2bit_1_out_3));
  not not_25 (not_25_out, in_6);
  not not_26 (not_26_out, Z);
  not not_27 (not_27_out, N);
  not not_28 (not_28_out, MODE_MOVE);
  not not_29 (not_29_out, in_6);
  not not_30 (not_30_out, and_2bit_1_out_3);
  AND_2bit and_2bit_1 (.in_1(MODE_MOVE), .in_2(in_6), .out_3(and_2bit_1_out_3));
  AND_2bit and_2bit_2 (.in_1(MODE_MOVE), .in_2(or_2bit_1_out_3), .out_3(and_2bit_2_out_3));
  AND_2bit and_2bit_3 (.in_1(and_14_out), .in_2(Z), .out_3(and_2bit_3_out_3));
  AND_2bit and_2bit_4 (.in_1(and_2bit_5_out_3), .in_2(JG_out), .out_3(and_2bit_4_out_3));
  AND_2bit and_2bit_5 (.in_1(not_26_out), .in_2(not_27_out), .out_3(and_2bit_5_out_3));
  AND_2bit and_2bit_6 (.in_1(JGE_out), .in_2(not_27_out), .out_3(and_2bit_6_out_3));
  AND_2bit and_2bit_7 (.in_1(N), .in_2(JL_out), .out_3(and_2bit_7_out_3));
  AND_2bit and_2bit_8 (.in_1(N), .in_2(JLE_out), .out_3(and_2bit_8_out_3));
  AND_2bit and_2bit_9 (.in_1(and_2bit_8_out_3), .in_2(Z), .out_3(and_2bit_9_out_3));
  and and_15 (and_15_out, and_2_out, not_28_out, not_29_out);
  and and_16 (and_16_out, and_2_out, not_28_out, in_6);
  and and_17 (and_17_out, and_2_out, not_29_out, MODE_MOVE);
  not not_31 (not_31_out, in_1);
  not not_32 (not_32_out, in_2);
  not not_33 (not_33_out, in_3);
  not not_34 (not_34_out, in_4);
  or or_4 (or_4_out, and_13_out, and_2bit_3_out_3, and_2bit_4_out_3, and_2bit_6_out_3, and_2bit_7_out_3);
  and and_18 (and_18_out, not_31_out, not_32_out, not_33_out, not_34_out, not_30_out);
  and and_19 (and_19_out, in_4, not_33_out, not_32_out, not_31_out);
  and and_20 (and_20_out, in_3, not_34_out, not_32_out, not_31_out);
  and and_21 (and_21_out, in_4, in_3, not_32_out, not_31_out);
  and and_22 (and_22_out, in_2, not_33_out, not_31_out, not_34_out);
  and and_23 (and_23_out, in_3, not_31_out, in_2, not_34_out);
  and and_24 (and_24_out, in_4, in_3, in_2, not_31_out);
  and and_25 (and_25_out, in_4, not_33_out, in_2, not_31_out);
  OR_2Bit or_2bit_2 (.in_1(and_2bit_9_out_3), .in_2(or_4_out), .out_3(JUMP));
  or or_5 (or_5_out, and_18_out, and_19_out, and_20_out, and_21_out, and_22_out);
  or or_6 (or_6_out, and_23_out, and_24_out, and_25_out);
  or or_7 (Stc_D, or_5_out, or_6_out);
  not not_35 (stc_RAM, not_30_out);
  AND_2bit and_2bit_10 (.in_1(and_2bit_2_out_3), .in_2(and_2_out), .out_3(SEL_ADDR));
  or or_8 (or_8_out, out_9, SEL_ALU, out_11);
  OR_2Bit or_2bit_3 (.in_1(and_3_out), .in_2(or_8_out), .out_3(or_2bit_3_out_3));
  MUX_CU mux_cu_1 (
    .in_1(or_2bit_3_out_3), .in_2(and_15_out), .in_3(and_16_out), .in_4(and_17_out), .out_5(SEL_SRC),
    .out_6(out_18));

  // Notes on the sheet:
  //   JUMP
  //   JE
  //   MOVE 01 REG
  //   MOVE 10IMM
  //   MOVE 11 MEM
  //   ALU
endmodule

module MUX_RS (
  input  in_1,
  input  D1,
  input  in_3,
  input  in_4,
  input  in_5,
  input  in_6,
  input  in_7,
  input  in_8,
  input  in_9,
  input  in_10,
  input  D2,
  input  in_12,
  input  in_13,
  input  in_14,
  input  in_15,
  input  in_16,
  input  in_17,
  input  in_18,
  input  D3,
  input  in_20,
  input  in_21,
  input  in_22,
  input  in_23,
  input  in_24,
  input  in_25,
  input  in_26,
  input  D4,
  input  in_28,
  input  in_29,
  input  in_30,
  input  in_31,
  input  in_32,
  input  in_33,
  input  in_34,
  output out_35,
  output out_36,
  output out_37,
  output out_38,
  output out_39,
  output out_40,
  output out_41,
  output out_42
);

  wire and_2bit_1_out_3, and_2bit_2_out_3, and_2bit_3_out_3, and_2bit_4_out_3, and_2bit_5_out_3,
       and_2bit_6_out_3, and_2bit_7_out_3, and_2bit_8_out_3, and_2bit_9_out_3, and_2bit_10_out_3,
       and_2bit_11_out_3, and_2bit_12_out_3, and_2bit_13_out_3, and_2bit_14_out_3, and_2bit_15_out_3,
       and_2bit_16_out_3, and_2bit_17_out_3, and_2bit_18_out_3, and_2bit_19_out_3, and_2bit_20_out_3,
       and_2bit_21_out_3, and_2bit_22_out_3, and_2bit_23_out_3, and_2bit_24_out_3, and_2bit_25_out_3,
       and_2bit_26_out_3, and_2bit_27_out_3, and_2bit_28_out_3, and_2bit_29_out_3, and_2bit_30_out_3,
       and_2bit_31_out_3, and_2bit_32_out_3, and_2bit_33_out_3, and_2bit_34_out_3, and_2bit_35_out_3,
       and_2bit_36_out_3, not_1_out, not_2_out;

  AND_2bit and_2bit_1 (.in_1(not_1_out), .in_2(not_2_out), .out_3(and_2bit_1_out_3));
  not not_1 (not_1_out, in_33);
  not not_2 (not_2_out, in_34);
  AND_2bit and_2bit_2 (.in_1(in_33), .in_2(not_2_out), .out_3(and_2bit_2_out_3));
  AND_2bit and_2bit_3 (.in_1(not_1_out), .in_2(in_34), .out_3(and_2bit_3_out_3));
  AND_2bit and_2bit_4 (.in_1(in_33), .in_2(in_34), .out_3(and_2bit_4_out_3));
  AND_2bit and_2bit_5 (.in_1(and_2bit_1_out_3), .in_2(D1), .out_3(and_2bit_5_out_3));
  AND_2bit and_2bit_6 (.in_1(in_1), .in_2(and_2bit_1_out_3), .out_3(and_2bit_6_out_3));
  AND_2bit and_2bit_7 (.in_1(and_2bit_1_out_3), .in_2(in_3), .out_3(and_2bit_7_out_3));
  AND_2bit and_2bit_8 (.in_1(in_4), .in_2(and_2bit_1_out_3), .out_3(and_2bit_8_out_3));
  AND_2bit and_2bit_9 (.in_1(in_7), .in_2(and_2bit_1_out_3), .out_3(and_2bit_9_out_3));
  AND_2bit and_2bit_10 (.in_1(in_6), .in_2(and_2bit_1_out_3), .out_3(and_2bit_10_out_3));
  AND_2bit and_2bit_11 (.in_1(in_5), .in_2(and_2bit_1_out_3), .out_3(and_2bit_11_out_3));
  or or_1 (out_35, and_2bit_6_out_3, and_2bit_13_out_3, and_2bit_22_out_3, and_2bit_29_out_3);
  AND_2bit and_2bit_12 (.in_1(in_8), .in_2(and_2bit_1_out_3), .out_3(and_2bit_12_out_3));
  AND_2bit and_2bit_13 (.in_1(in_9), .in_2(and_2bit_2_out_3), .out_3(and_2bit_13_out_3));
  AND_2bit and_2bit_14 (.in_1(and_2bit_2_out_3), .in_2(D2), .out_3(and_2bit_14_out_3));
  AND_2bit and_2bit_15 (.in_1(and_2bit_2_out_3), .in_2(in_10), .out_3(and_2bit_15_out_3));
  or or_2 (out_36, and_2bit_5_out_3, and_2bit_15_out_3, and_2bit_21_out_3, and_2bit_30_out_3);
  AND_2bit and_2bit_16 (.in_1(in_14), .in_2(and_2bit_2_out_3), .out_3(and_2bit_16_out_3));
  AND_2bit and_2bit_17 (.in_1(in_12), .in_2(and_2bit_2_out_3), .out_3(and_2bit_17_out_3));
  AND_2bit and_2bit_18 (.in_1(in_13), .in_2(and_2bit_2_out_3), .out_3(and_2bit_18_out_3));
  or or_3 (out_37, and_2bit_7_out_3, and_2bit_14_out_3, and_2bit_24_out_3, and_2bit_31_out_3);
  AND_2bit and_2bit_19 (.in_1(in_16), .in_2(and_2bit_2_out_3), .out_3(and_2bit_19_out_3));
  AND_2bit and_2bit_20 (.in_1(in_15), .in_2(and_2bit_2_out_3), .out_3(and_2bit_20_out_3));
  AND_2bit and_2bit_21 (.in_1(and_2bit_3_out_3), .in_2(in_18), .out_3(and_2bit_21_out_3));
  AND_2bit and_2bit_22 (.in_1(in_17), .in_2(and_2bit_3_out_3), .out_3(and_2bit_22_out_3));
  or or_4 (out_38, and_2bit_8_out_3, and_2bit_17_out_3, and_2bit_23_out_3, and_2bit_32_out_3);
  AND_2bit and_2bit_23 (.in_1(in_20), .in_2(and_2bit_3_out_3), .out_3(and_2bit_23_out_3));
  AND_2bit and_2bit_24 (.in_1(and_2bit_3_out_3), .in_2(D3), .out_3(and_2bit_24_out_3));
  or or_5 (out_39, and_2bit_11_out_3, and_2bit_27_out_3, and_2bit_18_out_3, and_2bit_34_out_3);
  AND_2bit and_2bit_25 (.in_1(in_22), .in_2(and_2bit_3_out_3), .out_3(and_2bit_25_out_3));
  AND_2bit and_2bit_26 (.in_1(in_23), .in_2(and_2bit_3_out_3), .out_3(and_2bit_26_out_3));
  AND_2bit and_2bit_27 (.in_1(in_21), .in_2(and_2bit_3_out_3), .out_3(and_2bit_27_out_3));
  AND_2bit and_2bit_28 (.in_1(in_24), .in_2(and_2bit_3_out_3), .out_3(and_2bit_28_out_3));
  AND_2bit and_2bit_29 (.in_1(in_25), .in_2(and_2bit_4_out_3), .out_3(and_2bit_29_out_3));
  or or_6 (out_40, and_2bit_10_out_3, and_2bit_16_out_3, and_2bit_25_out_3, and_2bit_33_out_3);
  AND_2bit and_2bit_30 (.in_1(and_2bit_4_out_3), .in_2(in_26), .out_3(and_2bit_30_out_3));
  AND_2bit and_2bit_31 (.in_1(and_2bit_4_out_3), .in_2(D4), .out_3(and_2bit_31_out_3));
  or or_7 (out_41, and_2bit_9_out_3, and_2bit_20_out_3, and_2bit_26_out_3, and_2bit_35_out_3);
  AND_2bit and_2bit_32 (.in_1(in_28), .in_2(and_2bit_4_out_3), .out_3(and_2bit_32_out_3));
  AND_2bit and_2bit_33 (.in_1(in_30), .in_2(and_2bit_4_out_3), .out_3(and_2bit_33_out_3));
  AND_2bit and_2bit_34 (.in_1(in_29), .in_2(and_2bit_4_out_3), .out_3(and_2bit_34_out_3));
  AND_2bit and_2bit_35 (.in_1(in_31), .in_2(and_2bit_4_out_3), .out_3(and_2bit_35_out_3));
  AND_2bit and_2bit_36 (.in_1(in_32), .in_2(and_2bit_4_out_3), .out_3(and_2bit_36_out_3));
  or or_8 (out_42, and_2bit_19_out_3, and_2bit_12_out_3, and_2bit_28_out_3, and_2bit_36_out_3);
endmodule

module OR_2Bit (
  input  in_1,
  input  in_2,
  output out_3
);

  or or_1 (out_3, in_1, in_2);
endmodule

module MOVE_CIRCUIT (
  input  in_1,
  input  in_2,
  input  in_3,
  input  in_4,
  input  in_5,
  input  in_6,
  input  in_7,
  input  in_8,
  input  in_9,
  input  in_10,
  input  in_11,
  input  in_12,
  input  in_13,
  input  in_14,
  input  in_15,
  input  in_16,
  input  in_17,
  input  in_18,
  input  in_19,
  input  in_20,
  input  in_21,
  input  in_22,
  input  in_23,
  input  in_24,
  input  in_25,
  input  in_26,
  input  in_27,
  input  in_28,
  input  in_29,
  input  in_30,
  input  in_31,
  input  in_32,
  input  in_33,
  input  in_34,
  input  in_35,
  output M,
  output D,
  output out_38,
  output out_39,
  output out_40,
  output out_41,
  output out_42,
  output out_43,
  output out_44,
  output out_45
);

  wire and_2bit_1_out_3, and_2bit_2_out_3, and_2bit_3_out_3, and_2bit_5_out_3, and_2bit_6_out_3,
       and_2bit_7_out_3, and_2bit_8_out_3, and_2bit_9_out_3, and_2bit_10_out_3, and_2bit_11_out_3,
       and_2bit_13_out_3, and_2bit_14_out_3, and_2bit_15_out_3, and_2bit_16_out_3, and_2bit_18_out_3,
       and_2bit_19_out_3, and_2bit_20_out_3, and_2bit_21_out_3, and_2bit_22_out_3, and_2bit_25_out_3,
       and_2bit_26_out_3, and_2bit_28_out_3, and_2bit_29_out_3, and_2bit_30_out_3, and_2bit_31_out_3,
       and_2bit_32_out_3, and_2bit_33_out_3, and_2bit_34_out_3, and_2bit_36_out_3, and_2bit_37_out_3,
       and_2bit_39_out_3, and_2bit_40_out_3, and_2bit_41_out_3, and_2bit_42_out_3, and_2bit_43_out_3,
       not_1_out, not_2_out, or_1_out, or_2_out, or_3_out, or_4_out, or_5_out, or_6_out, or_7_out, or_8_out;

  not not_1 (not_1_out, in_33);
  AND_2bit and_2bit_1 (.in_1(not_1_out), .in_2(not_2_out), .out_3(and_2bit_1_out_3));
  not not_2 (not_2_out, in_34);
  AND_2bit and_2bit_2 (.in_1(in_33), .in_2(not_2_out), .out_3(and_2bit_2_out_3));
  AND_2bit and_2bit_3 (.in_1(not_1_out), .in_2(in_34), .out_3(and_2bit_3_out_3));
  AND_2bit and_2bit_4 (.in_1(in_33), .in_2(in_34), .out_3(M));
  AND_2bit and_2bit_5 (.in_1(and_2bit_1_out_3), .in_2(in_2), .out_3(and_2bit_5_out_3));
  AND_2bit and_2bit_6 (.in_1(in_1), .in_2(and_2bit_1_out_3), .out_3(and_2bit_6_out_3));
  AND_2bit and_2bit_7 (.in_1(and_2bit_1_out_3), .in_2(in_3), .out_3(and_2bit_7_out_3));
  AND_2bit and_2bit_8 (.in_1(in_4), .in_2(and_2bit_1_out_3), .out_3(and_2bit_8_out_3));
  AND_2bit and_2bit_9 (.in_1(in_5), .in_2(and_2bit_1_out_3), .out_3(and_2bit_9_out_3));
  AND_2bit and_2bit_10 (.in_1(in_7), .in_2(and_2bit_1_out_3), .out_3(and_2bit_10_out_3));
  AND_2bit and_2bit_11 (.in_1(in_6), .in_2(and_2bit_1_out_3), .out_3(and_2bit_11_out_3));
  or or_1 (or_1_out, and_2bit_6_out_3, and_2bit_15_out_3, and_2bit_25_out_3, and_2bit_33_out_3);
  AND_2bit and_2bit_12 (.in_1(in_35), .in_2(or_1_out), .out_3(out_38));
  AND_2bit and_2bit_13 (.in_1(in_8), .in_2(and_2bit_1_out_3), .out_3(and_2bit_13_out_3));
  AND_2bit and_2bit_14 (.in_1(and_2bit_2_out_3), .in_2(in_11), .out_3(and_2bit_14_out_3));
  AND_2bit and_2bit_15 (.in_1(in_9), .in_2(and_2bit_2_out_3), .out_3(and_2bit_15_out_3));
  AND_2bit and_2bit_16 (.in_1(and_2bit_2_out_3), .in_2(in_10), .out_3(and_2bit_16_out_3));
  or or_2 (or_2_out, and_2bit_5_out_3, and_2bit_16_out_3, and_2bit_26_out_3, and_2bit_36_out_3);
  AND_2bit and_2bit_17 (.in_1(in_35), .in_2(or_2_out), .out_3(out_39));
  AND_2bit and_2bit_18 (.in_1(in_13), .in_2(and_2bit_2_out_3), .out_3(and_2bit_18_out_3));
  AND_2bit and_2bit_19 (.in_1(in_12), .in_2(and_2bit_2_out_3), .out_3(and_2bit_19_out_3));
  AND_2bit and_2bit_20 (.in_1(in_14), .in_2(and_2bit_2_out_3), .out_3(and_2bit_20_out_3));
  or or_3 (or_3_out, and_2bit_7_out_3, and_2bit_14_out_3, and_2bit_28_out_3, and_2bit_37_out_3);
  AND_2bit and_2bit_21 (.in_1(in_15), .in_2(and_2bit_2_out_3), .out_3(and_2bit_21_out_3));
  AND_2bit and_2bit_22 (.in_1(in_16), .in_2(and_2bit_2_out_3), .out_3(and_2bit_22_out_3));
  AND_2bit and_2bit_23 (.in_1(in_35), .in_2(or_3_out), .out_3(out_40));
  AND_2bit and_2bit_24 (.in_1(in_35), .in_2(or_4_out), .out_3(out_41));
  AND_2bit and_2bit_25 (.in_1(in_17), .in_2(and_2bit_3_out_3), .out_3(and_2bit_25_out_3));
  AND_2bit and_2bit_26 (.in_1(and_2bit_3_out_3), .in_2(in_18), .out_3(and_2bit_26_out_3));
  or or_4 (or_4_out, and_2bit_8_out_3, and_2bit_19_out_3, and_2bit_29_out_3, and_2bit_41_out_3);
  AND_2bit and_2bit_27 (.in_1(in_35), .in_2(or_5_out), .out_3(out_42));
  AND_2bit and_2bit_28 (.in_1(and_2bit_3_out_3), .in_2(in_19), .out_3(and_2bit_28_out_3));
  AND_2bit and_2bit_29 (.in_1(in_20), .in_2(and_2bit_3_out_3), .out_3(and_2bit_29_out_3));
  or or_5 (or_5_out, and_2bit_9_out_3, and_2bit_31_out_3, and_2bit_18_out_3, and_2bit_40_out_3);
  AND_2bit and_2bit_30 (.in_1(in_23), .in_2(and_2bit_3_out_3), .out_3(and_2bit_30_out_3));
  AND_2bit and_2bit_31 (.in_1(in_21), .in_2(and_2bit_3_out_3), .out_3(and_2bit_31_out_3));
  AND_2bit and_2bit_32 (.in_1(in_22), .in_2(and_2bit_3_out_3), .out_3(and_2bit_32_out_3));
  AND_2bit and_2bit_33 (.in_1(in_25), .in_2(M), .out_3(and_2bit_33_out_3));
  AND_2bit and_2bit_34 (.in_1(in_24), .in_2(and_2bit_3_out_3), .out_3(and_2bit_34_out_3));
  or or_6 (or_6_out, and_2bit_11_out_3, and_2bit_20_out_3, and_2bit_32_out_3, and_2bit_39_out_3);
  AND_2bit and_2bit_35 (.in_1(in_35), .in_2(or_6_out), .out_3(out_43));
  AND_2bit and_2bit_36 (.in_1(M), .in_2(in_26), .out_3(and_2bit_36_out_3));
  AND_2bit and_2bit_37 (.in_1(M), .in_2(in_27), .out_3(and_2bit_37_out_3));
  or or_7 (or_7_out, and_2bit_10_out_3, and_2bit_21_out_3, and_2bit_30_out_3, and_2bit_42_out_3);
  AND_2bit and_2bit_38 (.in_1(in_35), .in_2(or_7_out), .out_3(out_44));
  AND_2bit and_2bit_39 (.in_1(in_30), .in_2(M), .out_3(and_2bit_39_out_3));
  AND_2bit and_2bit_40 (.in_1(in_29), .in_2(M), .out_3(and_2bit_40_out_3));
  AND_2bit and_2bit_41 (.in_1(in_28), .in_2(M), .out_3(and_2bit_41_out_3));
  AND_2bit and_2bit_42 (.in_1(in_31), .in_2(M), .out_3(and_2bit_42_out_3));
  AND_2bit and_2bit_43 (.in_1(in_32), .in_2(M), .out_3(and_2bit_43_out_3));
  or or_8 (or_8_out, and_2bit_22_out_3, and_2bit_13_out_3, and_2bit_34_out_3, and_2bit_43_out_3);
  AND_2bit and_2bit_44 (.in_1(in_35), .in_2(or_8_out), .out_3(out_45));
  or or_9 (D, and_2bit_3_out_3, and_2bit_1_out_3, and_2bit_2_out_3);
endmodule

module sel_RD (
  input  in_1,
  input  in_2,
  input  in_3,
  output out_4,
  output out_5,
  output out_6,
  output out_7
);

  wire decodeur_2bit_1_out_3, decodeur_2bit_1_out_4, decodeur_2bit_1_out_5, decodeur_2bit_1_out_6;

  and and_1 (out_4, in_3, decodeur_2bit_1_out_6);
  DECODEUR_2Bit decodeur_2bit_1 (
    .E0(in_2), .E1(in_1), .out_3(decodeur_2bit_1_out_3), .out_4(decodeur_2bit_1_out_4),
    .out_5(decodeur_2bit_1_out_5), .out_6(decodeur_2bit_1_out_6));
  and and_2 (out_6, in_3, decodeur_2bit_1_out_4);
  and and_3 (out_5, in_3, decodeur_2bit_1_out_5);
  and and_4 (out_7, in_3, decodeur_2bit_1_out_3);
endmodule

module CPU (
  input  in_1,
  output out_2,
  output out_3,
  output out_4,
  output out_5,
  output out_6,
  output out_7,
  output out_8,
  output out_9,
  output out_10,
  output out_11,
  output out_12,
  output out_13,
  output out_14,
  output out_15,
  output out_16,
  output out_17,
  output IR_REGISTER,
  output out_19,
  output out_20,
  output out_21,
  output out_22,
  output out_23,
  output out_24,
  output out_25,
  output out_26,
  output out_27,
  output out_28,
  output out_29,
  output out_30,
  output out_31,
  output out_32,
  output out_33,
  output out_34,
  output out_35,
  output out_36,
  output out_37,
  output out_38,
  output out_39,
  output out_40,
  output out_41,
  output out_42,
  output out_43,
  output out_44,
  output out_45,
  output out_46,
  output out_47,
  output out_48,
  output out_49,
  output out_50,
  output out_51,
  output out_52,
  output out_53,
  output out_54,
  output out_55,
  output out_56,
  output C,
  output out_58,
  output Z,
  output N,
  output V
);

  wire add008_1_c, add008_1_s0, add008_1_s1, add008_1_s2, add008_1_s3, add008_1_s4, add008_1_s5, add008_1_s6,
       add008_1_s7, and008_1_out_17, and008_1_out_18, and008_1_out_19, and008_1_out_20, and008_1_out_21,
       and008_1_out_22, and008_1_out_23, and008_1_out_24, and008_2_out_17, and008_2_out_18, and008_2_out_19,
       and008_2_out_20, and008_2_out_21, and008_2_out_22, and008_2_out_23, and008_2_out_24, and_2bit_1_out_3,
       and_selective_1_out_18, and_selective_1_out_19, and_selective_1_out_20, and_selective_1_out_21,
       and_selective_1_out_22, and_selective_1_out_23, and_selective_1_out_24, and_selective_1_out_25,
       and_selective_1_out_26, and_selective_1_out_27, and_selective_1_out_28, and_selective_1_out_29,
       and_selective_1_out_30, and_selective_1_out_31, and_selective_1_out_32, and_selective_1_out_33,
       and_selective_2_out_18, and_selective_2_out_19, and_selective_2_out_20, and_selective_2_out_21,
       and_selective_2_out_22, and_selective_2_out_23, and_selective_2_out_24, and_selective_2_out_25,
       and_selective_2_out_26, and_selective_2_out_27, and_selective_2_out_28, and_selective_2_out_29,
       and_selective_2_out_30, and_selective_2_out_31, and_selective_2_out_32, and_selective_2_out_33,
       and_selective_3_out_18, and_selective_3_out_19, and_selective_3_out_20, and_selective_3_out_21,
       and_selective_3_out_22, and_selective_3_out_23, and_selective_3_out_24, and_selective_3_out_25,
       and_selective_3_out_26, and_selective_3_out_27, and_selective_3_out_28, and_selective_3_out_29,
       and_selective_3_out_30, and_selective_3_out_31, and_selective_3_out_32, and_selective_3_out_33,
       and_selective_4_out_18, and_selective_4_out_19, and_selective_4_out_20, and_selective_4_out_21,
       and_selective_4_out_22, and_selective_4_out_23, and_selective_4_out_24, and_selective_4_out_25,
       and_selective_4_out_26, and_selective_4_out_27, and_selective_4_out_28, and_selective_4_out_29,
       and_selective_4_out_30, and_selective_4_out_31, and_selective_4_out_32, and_selective_4_out_33,
       clock_1_out, decodeur_3bit_1_s0, decodeur_3bit_1_s1, decodeur_3bit_1_s2, decodeur_3bit_1_s3,
       decodeur_3bit_1_s4, decodeur_3bit_1_s5, decodeur_3bit_1_s7, mul_pc_1_out_18, mul_pc_1_out_19,
       mul_pc_1_out_20, mul_pc_1_out_21, mul_pc_1_out_22, mul_pc_1_out_23, mul_pc_1_out_24, mul_pc_1_out_25,
       mul_pc_3_out_18, mul_pc_3_out_19, mul_pc_3_out_20, mul_pc_3_out_21, mul_pc_3_out_22, mul_pc_3_out_23,
       mul_pc_3_out_24, mul_pc_3_out_25, mux_mode_1_out_7, mux_rs_1_out_35, mux_rs_1_out_36, mux_rs_1_out_37,
       mux_rs_1_out_38, mux_rs_1_out_39, mux_rs_1_out_40, mux_rs_1_out_41, mux_rs_1_out_42, mux_rs_2_out_35,
       mux_rs_2_out_36, mux_rs_2_out_37, mux_rs_2_out_38, mux_rs_2_out_39, mux_rs_2_out_40, mux_rs_2_out_41,
       mux_rs_2_out_42, mux_rs_3_out_35, mux_rs_3_out_36, mux_rs_3_out_37, mux_rs_3_out_38, mux_rs_3_out_39,
       mux_rs_3_out_40, mux_rs_3_out_41, mux_rs_3_out_42, mux_we_1_out_4, mux_we_1_out_5, mux_we_1_out_6,
       mux_we_1_out_7, not008_1_out_10, not008_1_out_11, not008_1_out_12, not008_1_out_13, not008_1_out_14,
       not008_1_out_15, not008_1_out_16, not008_1_out_17, not_1_out, not_2_out, not_3_out,
       opcode_circuit_1_hlt, opcode_circuit_1_jump, opcode_circuit_1_out_18, opcode_circuit_1_sel_addr,
       opcode_circuit_1_sel_src, opcode_circuit_1_stc_d, opcode_circuit_1_stc_ram, or008_1_o0, or008_1_o1,
       or008_1_o2, or008_1_o3, or008_1_o4, or008_1_o5, or008_1_o6, or008_1_o7, or_1_out, overflow_1_out_4,
       pc_add_1_out_9, pc_add_1_out_10, pc_add_1_out_11, pc_add_1_out_12, pc_add_1_out_13, pc_add_1_out_14,
       pc_add_1_out_15, pc_add_1_out_16, shl_1_c, shl_1_out_12, shl_1_out_13, shl_1_out_14, shl_1_out_15,
       shl_1_out_16, shl_1_out_18, shl_1_s0, shl_1_s7, shr_1_c, shr_1_out_12, shr_1_out_13, shr_1_out_14,
       shr_1_out_15, shr_1_out_16, shr_1_out_18, shr_1_s0, shr_1_s7, zero_1_out_9;
  wire [1:0] mux_sel_rd_1_out_10, mux_sel_rd_2_out_10;
  wire [2:0] opcode_circuit_1_out_11;
  wire [7:0] flip_flop_d_8bit_1_out_19, mul_pc_2_out_18;
  wire [15:0] ram_1_data;

  Flip_Flop_D_8bit flip_flop_d_8bit_1 (
    .H(and_2bit_1_out_3), .S(1'b1), .R(in_1), .in_1(mul_pc_1_out_25), .in_2(mul_pc_1_out_24),
    .in_3(mul_pc_1_out_23), .in_4(mul_pc_1_out_22), .in_5(mul_pc_1_out_21), .in_6(mul_pc_1_out_20),
    .in_7(mul_pc_1_out_19), .in_8(mul_pc_1_out_18), .out_12(flip_flop_d_8bit_1_out_19[7]),
    .out_13(flip_flop_d_8bit_1_out_19[6]), .out_14(flip_flop_d_8bit_1_out_19[5]),
    .out_15(flip_flop_d_8bit_1_out_19[4]), .out_16(flip_flop_d_8bit_1_out_19[3]),
    .out_17(flip_flop_d_8bit_1_out_19[2]), .out_18(flip_flop_d_8bit_1_out_19[1]),
    .out_19(flip_flop_d_8bit_1_out_19[0]));
  PC_ADD pc_add_1 (
    .in_1(flip_flop_d_8bit_1_out_19[7]), .in_2(flip_flop_d_8bit_1_out_19[6]),
    .in_3(flip_flop_d_8bit_1_out_19[5]), .in_4(flip_flop_d_8bit_1_out_19[4]),
    .in_5(flip_flop_d_8bit_1_out_19[3]), .in_6(flip_flop_d_8bit_1_out_19[2]),
    .in_7(flip_flop_d_8bit_1_out_19[1]), .in_8(flip_flop_d_8bit_1_out_19[0]), .out_9(pc_add_1_out_9),
    .out_10(pc_add_1_out_10), .out_11(pc_add_1_out_11), .out_12(pc_add_1_out_12), .out_13(pc_add_1_out_13),
    .out_14(pc_add_1_out_14), .out_15(pc_add_1_out_15), .out_16(pc_add_1_out_16));
  MUL_PC mul_pc_1 (
    .in_1(pc_add_1_out_16), .in_2(pc_add_1_out_15), .in_3(pc_add_1_out_14), .PC_1(pc_add_1_out_13),
    .in_5(pc_add_1_out_12), .in_6(pc_add_1_out_11), .in_7(pc_add_1_out_10), .in_8(pc_add_1_out_9),
    .in_9(out_33), .in_10(out_32), .JUMP(out_31), .in_12(out_30), .in_13(out_29), .in_14(out_28),
    .in_15(out_27), .in_16(out_26), .in_17(opcode_circuit_1_jump), .out_18(mul_pc_1_out_18),
    .out_19(mul_pc_1_out_19), .out_20(mul_pc_1_out_20), .out_21(mul_pc_1_out_21), .out_22(mul_pc_1_out_22),
    .out_23(mul_pc_1_out_23), .out_24(mul_pc_1_out_24), .out_25(mul_pc_1_out_25));
  RAM #(.dataWidth(16)) ram_1 (
    .addr(mul_pc_2_out_18), .data(ram_1_data), .sel(1'b1), .clk(and_2bit_1_out_3), .ld(not_1_out), .clr(1'b0));
  not not_1 (not_1_out, opcode_circuit_1_stc_ram);
  MUX_SEL_RD mux_sel_rd_1 (
    .in_5(out_21), .in_6(out_20), .in_7(out_19), .in_8(IR_REGISTER), .ALU(out_23), .in_2(out_24),
    .MOVE(out_24), .in_4(out_25), .out_9(mux_sel_rd_1_out_10[1]), .out_10(mux_sel_rd_1_out_10[0]));
  MUX_SEL_RD mux_sel_rd_2 (
    .in_5(out_21), .in_6(out_20), .in_7(out_19), .in_8(IR_REGISTER), .ALU(out_25), .in_2(out_26),
    .MOVE(out_26), .in_4(out_27), .out_9(mux_sel_rd_2_out_10[1]), .out_10(mux_sel_rd_2_out_10[0]));
  Flip_Flop_D_16bit flip_flop_d_16bit_1 (
    .H(and_2bit_1_out_3), .S(1'b1), .R(1'b0), .in_1(ram_1_data[15]), .in_2(ram_1_data[14]),
    .in_3(ram_1_data[13]), .in_4(ram_1_data[12]), .in_5(ram_1_data[11]), .in_6(ram_1_data[10]),
    .in_7(ram_1_data[9]), .in_8(ram_1_data[8]), .in_9(ram_1_data[7]), .in_10(ram_1_data[6]),
    .in_11(ram_1_data[5]), .in_12(ram_1_data[4]), .in_13(ram_1_data[3]), .in_14(ram_1_data[2]),
    .in_15(ram_1_data[1]), .in_16(ram_1_data[0]), .out_20(IR_REGISTER), .out_21(out_19), .out_22(out_20),
    .out_23(out_21), .out_24(out_22), .out_25(out_23), .out_26(out_24), .out_27(out_25), .out_28(out_26),
    .out_29(out_27), .out_30(out_28), .out_31(out_29), .out_32(out_30), .out_33(out_31), .out_34(out_32),
    .out_35(out_33));
  OPCODE_CIRCUIT opcode_circuit_1 (
    .in_1(IR_REGISTER), .in_2(out_19), .in_3(out_20), .in_4(out_21), .MODE_MOVE(out_22), .in_6(out_23),
    .Z(Z), .N(N), .out_9(opcode_circuit_1_out_11[2]), .SEL_ALU(opcode_circuit_1_out_11[1]),
    .out_11(opcode_circuit_1_out_11[0]), .Stc_D(opcode_circuit_1_stc_d), .JUMP(opcode_circuit_1_jump),
    .stc_RAM(opcode_circuit_1_stc_ram), .SEL_ADDR(opcode_circuit_1_sel_addr), .HLT(opcode_circuit_1_hlt),
    .SEL_SRC(opcode_circuit_1_sel_src), .out_18(opcode_circuit_1_out_18));
  MUX_MODE mux_mode_1 (
    .in_3(out_21), .in_4(out_20), .in_5(out_19), .in_6(IR_REGISTER), .in_1(out_22), .in_2(out_23),
    .out_7(mux_mode_1_out_7));
  MUX_WE mux_we_1 (
    ._1(mux_sel_rd_1_out_10[1]), ._0(mux_sel_rd_1_out_10[0]), .WE_D(opcode_circuit_1_stc_d),
    .out_4(mux_we_1_out_4), .out_5(mux_we_1_out_5), .out_6(mux_we_1_out_6), .out_7(mux_we_1_out_7));
  MUL_PC mul_pc_2 (
    .in_1(flip_flop_d_8bit_1_out_19[0]), .in_2(flip_flop_d_8bit_1_out_19[1]),
    .in_3(flip_flop_d_8bit_1_out_19[2]), .PC_1(flip_flop_d_8bit_1_out_19[3]),
    .in_5(flip_flop_d_8bit_1_out_19[4]), .in_6(flip_flop_d_8bit_1_out_19[5]),
    .in_7(flip_flop_d_8bit_1_out_19[6]), .in_8(flip_flop_d_8bit_1_out_19[7]), .in_9(out_33), .in_10(out_32),
    .JUMP(out_31), .in_12(out_30), .in_13(out_29), .in_14(out_28), .in_15(out_27), .in_16(out_26),
    .in_17(opcode_circuit_1_sel_addr), .out_18(mul_pc_2_out_18[0]), .out_19(mul_pc_2_out_18[1]),
    .out_20(mul_pc_2_out_18[2]), .out_21(mul_pc_2_out_18[3]), .out_22(mul_pc_2_out_18[4]),
    .out_23(mul_pc_2_out_18[5]), .out_24(mul_pc_2_out_18[6]), .out_25(mul_pc_2_out_18[7]));
  not not_2 (not_2_out, opcode_circuit_1_hlt);
  Clock clock_1 (.out(clock_1_out));
  AND_2bit and_2bit_1 (.in_1(clock_1_out), .in_2(not_2_out), .out_3(and_2bit_1_out_3));
  Flip_Flop_D_8bit flip_flop_d_8bit_2 (
    .H(and_2bit_1_out_3), .S(mux_we_1_out_7), .R(1'b0), .in_1(mux_rs_2_out_42), .in_2(mux_rs_2_out_41),
    .in_3(mux_rs_2_out_40), .in_4(mux_rs_2_out_39), .in_5(mux_rs_2_out_38), .in_6(mux_rs_2_out_37),
    .in_7(mux_rs_2_out_36), .in_8(mux_rs_2_out_35), .out_12(out_2), .out_13(out_3), .out_14(out_4),
    .out_15(out_5), .out_16(out_6), .out_17(out_7), .out_18(out_8), .out_19(out_9));
  Flip_Flop_D_8bit flip_flop_d_8bit_3 (
    .H(and_2bit_1_out_3), .S(mux_we_1_out_6), .R(1'b0), .in_1(mux_rs_2_out_42), .in_2(mux_rs_2_out_41),
    .in_3(mux_rs_2_out_40), .in_4(mux_rs_2_out_39), .in_5(mux_rs_2_out_38), .in_6(mux_rs_2_out_37),
    .in_7(mux_rs_2_out_36), .in_8(mux_rs_2_out_35), .out_12(out_10), .out_13(out_11), .out_14(out_12),
    .out_15(out_13), .out_16(out_14), .out_17(out_15), .out_18(out_16), .out_19(out_17));
  Flip_Flop_D_8bit flip_flop_d_8bit_4 (
    .H(and_2bit_1_out_3), .S(mux_we_1_out_5), .R(1'b0), .in_1(mux_rs_2_out_42), .in_2(mux_rs_2_out_41),
    .in_3(mux_rs_2_out_40), .in_4(mux_rs_2_out_39), .in_5(mux_rs_2_out_38), .in_6(mux_rs_2_out_37),
    .in_7(mux_rs_2_out_36), .in_8(mux_rs_2_out_35), .out_12(out_34), .out_13(out_35), .out_14(out_36),
    .out_15(out_37), .out_16(out_38), .out_17(out_39), .out_18(out_40), .out_19(out_41));
  Flip_Flop_D_8bit flip_flop_d_8bit_5 (
    .H(and_2bit_1_out_3), .S(mux_we_1_out_4), .R(1'b0), .in_1(mux_rs_2_out_42), .in_2(mux_rs_2_out_41),
    .in_3(mux_rs_2_out_40), .in_4(mux_rs_2_out_39), .in_5(mux_rs_2_out_38), .in_6(mux_rs_2_out_37),
    .in_7(mux_rs_2_out_36), .in_8(mux_rs_2_out_35), .out_12(out_42), .out_13(out_43), .out_14(out_44),
    .out_15(out_45), .out_16(out_46), .out_17(out_47), .out_18(out_48), .out_19(out_49));
  MUX_RS mux_rs_1 (
    .in_33(mux_sel_rd_1_out_10[0]), .in_34(mux_sel_rd_1_out_10[1]), .in_1(out_2), .D1(out_3), .in_3(out_4),
    .in_4(out_5), .in_5(out_6), .in_6(out_7), .in_7(out_8), .in_8(out_9), .in_9(out_10), .in_10(out_11),
    .D2(out_12), .in_12(out_13), .in_13(out_14), .in_14(out_15), .in_15(out_16), .in_16(out_17),
    .in_17(out_34), .in_18(out_35), .D3(out_36), .in_20(out_37), .in_21(out_38), .in_22(out_39),
    .in_23(out_40), .in_24(out_41), .in_25(out_42), .in_26(out_43), .D4(out_44), .in_28(out_45),
    .in_29(out_46), .in_30(out_47), .in_31(out_48), .in_32(out_49), .out_35(mux_rs_1_out_35),
    .out_36(mux_rs_1_out_36), .out_37(mux_rs_1_out_37), .out_38(mux_rs_1_out_38), .out_39(mux_rs_1_out_39),
    .out_40(mux_rs_1_out_40), .out_41(mux_rs_1_out_41), .out_42(mux_rs_1_out_42));
  MUX_RS mux_rs_2 (
    .in_33(opcode_circuit_1_sel_src), .in_34(opcode_circuit_1_out_18), .in_1(out_58), .D1(out_56),
    .in_3(out_55), .in_4(out_54), .in_5(out_53), .in_6(out_52), .in_7(out_51), .in_8(out_50),
    .in_9(mul_pc_3_out_18), .in_10(mul_pc_3_out_19), .D2(mul_pc_3_out_20), .in_12(mul_pc_3_out_21),
    .in_13(mul_pc_3_out_22), .in_14(mul_pc_3_out_23), .in_15(mul_pc_3_out_24), .in_16(mul_pc_3_out_25),
    .in_17(out_33), .in_18(out_32), .D3(out_31), .in_20(out_30), .in_21(out_29), .in_22(out_28),
    .in_23(out_27), .in_24(out_26), .in_25(ram_1_data[0]), .in_26(ram_1_data[1]), .D4(ram_1_data[2]),
    .in_28(ram_1_data[3]), .in_29(ram_1_data[4]), .in_30(ram_1_data[5]), .in_31(ram_1_data[6]),
    .in_32(ram_1_data[7]), .out_35(mux_rs_2_out_35), .out_36(mux_rs_2_out_36), .out_37(mux_rs_2_out_37),
    .out_38(mux_rs_2_out_38), .out_39(mux_rs_2_out_39), .out_40(mux_rs_2_out_40), .out_41(mux_rs_2_out_41),
    .out_42(mux_rs_2_out_42));
  DECODEUR_3Bit decodeur_3bit_1 (
    .e1(opcode_circuit_1_out_11[0]), .e2(opcode_circuit_1_out_11[1]), .e3(opcode_circuit_1_out_11[2]),
    .s0(decodeur_3bit_1_s0), .s1(decodeur_3bit_1_s1), .s2(decodeur_3bit_1_s2), .s3(decodeur_3bit_1_s3),
    .s4(decodeur_3bit_1_s4), .s5(decodeur_3bit_1_s5), .s7(decodeur_3bit_1_s7));
  MUX_RS mux_rs_3 (
    .in_33(mux_sel_rd_2_out_10[0]), .in_34(mux_sel_rd_2_out_10[1]), .in_1(out_2), .D1(out_3), .in_3(out_4),
    .in_4(out_5), .in_5(out_6), .in_6(out_7), .in_7(out_8), .in_8(out_9), .in_9(out_10), .in_10(out_11),
    .D2(out_12), .in_12(out_13), .in_13(out_14), .in_14(out_15), .in_15(out_16), .in_16(out_17),
    .in_17(out_34), .in_18(out_35), .D3(out_36), .in_20(out_37), .in_21(out_38), .in_22(out_39),
    .in_23(out_40), .in_24(out_41), .in_25(out_42), .in_26(out_43), .D4(out_44), .in_28(out_45),
    .in_29(out_46), .in_30(out_47), .in_31(out_48), .in_32(out_49), .out_35(mux_rs_3_out_35),
    .out_36(mux_rs_3_out_36), .out_37(mux_rs_3_out_37), .out_38(mux_rs_3_out_38), .out_39(mux_rs_3_out_39),
    .out_40(mux_rs_3_out_40), .out_41(mux_rs_3_out_41), .out_42(mux_rs_3_out_42));
  not not_3 (not_3_out, mux_mode_1_out_7);
  MUL_PC mul_pc_3 (
    .in_1(out_33), .in_2(out_32), .in_3(out_31), .PC_1(out_30), .in_5(out_29), .in_6(out_28), .in_7(out_27),
    .in_8(out_26), .in_9(mux_rs_3_out_42), .in_10(mux_rs_3_out_41), .JUMP(mux_rs_3_out_40),
    .in_12(mux_rs_3_out_39), .in_13(mux_rs_3_out_38), .in_14(mux_rs_3_out_37), .in_15(mux_rs_3_out_36),
    .in_16(mux_rs_3_out_35), .in_17(not_3_out), .out_18(mul_pc_3_out_18), .out_19(mul_pc_3_out_19),
    .out_20(mul_pc_3_out_20), .out_21(mul_pc_3_out_21), .out_22(mul_pc_3_out_22), .out_23(mul_pc_3_out_23),
    .out_24(mul_pc_3_out_24), .out_25(mul_pc_3_out_25));
  AND_Selective and_selective_1 (
    .A7(mux_rs_1_out_35), .A6(mux_rs_1_out_36), .A5(mux_rs_1_out_37), .A4(mux_rs_1_out_38),
    .A3(mux_rs_1_out_39), .A2(mux_rs_1_out_40), .A1(mux_rs_1_out_41), .A0(mux_rs_1_out_42),
    .B7(mul_pc_3_out_25), .B6(mul_pc_3_out_24), .B5(mul_pc_3_out_23), .B4(mul_pc_3_out_22),
    .B3(mul_pc_3_out_21), .B2(mul_pc_3_out_20), .B1(mul_pc_3_out_19), .B0(mul_pc_3_out_18),
    .Signal_D(decodeur_3bit_1_s0), .out_18(and_selective_1_out_18), .out_19(and_selective_1_out_19),
    .out_20(and_selective_1_out_20), .out_21(and_selective_1_out_21), .out_22(and_selective_1_out_22),
    .out_23(and_selective_1_out_23), .out_24(and_selective_1_out_24), .out_25(and_selective_1_out_25),
    .out_26(and_selective_1_out_26), .out_27(and_selective_1_out_27), .out_28(and_selective_1_out_28),
    .out_29(and_selective_1_out_29), .out_30(and_selective_1_out_30), .out_31(and_selective_1_out_31),
    .out_32(and_selective_1_out_32), .out_33(and_selective_1_out_33));
  AND_Selective and_selective_2 (
    .A7(mux_rs_1_out_35), .A6(mux_rs_1_out_36), .A5(mux_rs_1_out_37), .A4(mux_rs_1_out_38),
    .A3(mux_rs_1_out_39), .A2(mux_rs_1_out_40), .A1(mux_rs_1_out_41), .A0(mux_rs_1_out_42),
    .B7(mul_pc_3_out_25), .B6(mul_pc_3_out_24), .B5(mul_pc_3_out_23), .B4(mul_pc_3_out_22),
    .B3(mul_pc_3_out_21), .B2(mul_pc_3_out_20), .B1(mul_pc_3_out_19), .B0(mul_pc_3_out_18),
    .Signal_D(decodeur_3bit_1_s1), .out_18(and_selective_2_out_18), .out_19(and_selective_2_out_19),
    .out_20(and_selective_2_out_20), .out_21(and_selective_2_out_21), .out_22(and_selective_2_out_22),
    .out_23(and_selective_2_out_23), .out_24(and_selective_2_out_24), .out_25(and_selective_2_out_25),
    .out_26(and_selective_2_out_26), .out_27(and_selective_2_out_27), .out_28(and_selective_2_out_28),
    .out_29(and_selective_2_out_29), .out_30(and_selective_2_out_30), .out_31(and_selective_2_out_31),
    .out_32(and_selective_2_out_32), .out_33(and_selective_2_out_33));
  AND_Selective and_selective_3 (
    .A7(mux_rs_1_out_35), .A6(mux_rs_1_out_36), .A5(mux_rs_1_out_37), .A4(mux_rs_1_out_38),
    .A3(mux_rs_1_out_39), .A2(mux_rs_1_out_40), .A1(mux_rs_1_out_41), .A0(mux_rs_1_out_42),
    .B7(mul_pc_3_out_25), .B6(mul_pc_3_out_24), .B5(mul_pc_3_out_23), .B4(mul_pc_3_out_22),
    .B3(mul_pc_3_out_21), .B2(mul_pc_3_out_20), .B1(mul_pc_3_out_19), .B0(mul_pc_3_out_18),
    .Signal_D(decodeur_3bit_1_s2), .out_18(and_selective_3_out_18), .out_19(and_selective_3_out_19),
    .out_20(and_selective_3_out_20), .out_21(and_selective_3_out_21), .out_22(and_selective_3_out_22),
    .out_23(and_selective_3_out_23), .out_24(and_selective_3_out_24), .out_25(and_selective_3_out_25),
    .out_26(and_selective_3_out_26), .out_27(and_selective_3_out_27), .out_28(and_selective_3_out_28),
    .out_29(and_selective_3_out_29), .out_30(and_selective_3_out_30), .out_31(and_selective_3_out_31),
    .out_32(and_selective_3_out_32), .out_33(and_selective_3_out_33));
  AND_Selective and_selective_4 (
    .A7(mux_rs_1_out_35), .A6(mux_rs_1_out_36), .A5(mux_rs_1_out_37), .A4(mux_rs_1_out_38),
    .A3(mux_rs_1_out_39), .A2(mux_rs_1_out_40), .A1(mux_rs_1_out_41), .A0(mux_rs_1_out_42),
    .B7(mul_pc_3_out_25), .B6(mul_pc_3_out_24), .B5(mul_pc_3_out_23), .B4(mul_pc_3_out_22),
    .B3(mul_pc_3_out_21), .B2(mul_pc_3_out_20), .B1(mul_pc_3_out_19), .B0(mul_pc_3_out_18),
    .Signal_D(decodeur_3bit_1_s3), .out_18(and_selective_4_out_18), .out_19(and_selective_4_out_19),
    .out_20(and_selective_4_out_20), .out_21(and_selective_4_out_21), .out_22(and_selective_4_out_22),
    .out_23(and_selective_4_out_23), .out_24(and_selective_4_out_24), .out_25(and_selective_4_out_25),
    .out_26(and_selective_4_out_26), .out_27(and_selective_4_out_27), .out_28(and_selective_4_out_28),
    .out_29(and_selective_4_out_29), .out_30(and_selective_4_out_30), .out_31(and_selective_4_out_31),
    .out_32(and_selective_4_out_32), .out_33(and_selective_4_out_33));
  NOT008 not008_1 (
    .in_1(mux_rs_1_out_35), .in_2(mux_rs_1_out_36), .in_3(mux_rs_1_out_37), .in_4(mux_rs_1_out_38),
    .in_5(mux_rs_1_out_39), .in_6(mux_rs_1_out_40), .in_7(mux_rs_1_out_41), .in_8(mux_rs_1_out_42),
    .in_9(decodeur_3bit_1_s4), .out_10(not008_1_out_10), .out_11(not008_1_out_11), .out_12(not008_1_out_12),
    .out_13(not008_1_out_13), .out_14(not008_1_out_14), .out_15(not008_1_out_15), .out_16(not008_1_out_16),
    .out_17(not008_1_out_17));
  SHL shl_1 (
    .A7(mux_rs_1_out_35), .in_2(mux_rs_1_out_36), .in_3(mux_rs_1_out_37), .in_4(mux_rs_1_out_38),
    .in_5(mux_rs_1_out_39), .in_6(mux_rs_1_out_40), .A0(mux_rs_1_out_41), .in_8(mux_rs_1_out_42),
    .dec_com(decodeur_3bit_1_s5), .C(shl_1_c), .S7(shl_1_s7), .out_12(shl_1_out_12), .out_13(shl_1_out_13),
    .out_14(shl_1_out_14), .out_15(shl_1_out_15), .out_16(shl_1_out_16), .S0(shl_1_s0), .out_18(shl_1_out_18));
  SHR shr_1 (
    .A7(mux_rs_1_out_35), .in_2(mux_rs_1_out_36), .in_3(mux_rs_1_out_37), .in_4(mux_rs_1_out_38),
    .in_5(mux_rs_1_out_39), .in_6(mux_rs_1_out_40), .A0(mux_rs_1_out_41), .in_8(mux_rs_1_out_42),
    .dec_com(decodeur_3bit_1_s7), .C(shr_1_c), .S7(shr_1_s7), .out_12(shr_1_out_12), .out_13(shr_1_out_13),
    .out_14(shr_1_out_14), .out_15(shr_1_out_15), .out_16(shr_1_out_16), .S0(shr_1_s0), .out_18(shr_1_out_18));
  ADD008 add008_1 (
    .A7(and_selective_1_out_26), .A6(and_selective_1_out_27), .A5(and_selective_1_out_28),
    .A4(and_selective_1_out_29), .A3(and_selective_1_out_30), .A2(and_selective_1_out_31),
    .A1(and_selective_1_out_32), .A0(and_selective_1_out_33), .C(add008_1_c), .S7(add008_1_s7),
    .S6(add008_1_s6), .S5(add008_1_s5), .s4(add008_1_s4), .S3(add008_1_s3), .S2(add008_1_s2),
    .S1(add008_1_s1), .S0(add008_1_s0), .B7(and_selective_1_out_18), .B6(and_selective_1_out_19),
    .B5(and_selective_1_out_20), .B4(and_selective_1_out_21), .B3(and_selective_1_out_22),
    .B2(and_selective_1_out_23), .B1(and_selective_1_out_24), .B0(and_selective_1_out_25));
  AND008 and008_1 (
    .in_1(and_selective_2_out_26), .in_2(and_selective_2_out_27), .in_4(and_selective_2_out_28),
    .in_6(and_selective_2_out_29), .in_8(and_selective_2_out_30), .in_10(and_selective_2_out_31),
    .in_12(and_selective_2_out_32), .in_14(and_selective_2_out_33), .out_17(and008_1_out_17),
    .out_18(and008_1_out_18), .out_19(and008_1_out_19), .out_20(and008_1_out_20), .out_21(and008_1_out_21),
    .out_22(and008_1_out_22), .out_23(and008_1_out_23), .out_24(and008_1_out_24),
    .in_3(and_selective_2_out_18), .in_5(and_selective_2_out_19), .in_7(and_selective_2_out_20),
    .in_9(and_selective_2_out_21), .in_11(and_selective_2_out_22), .in_13(and_selective_2_out_23),
    .in_15(and_selective_2_out_24), .in_16(and_selective_2_out_25));
  OR008 or008_1 (
    .in_1(and_selective_3_out_26), .in_2(and_selective_3_out_27), .in_4(and_selective_3_out_28),
    .in_6(and_selective_3_out_29), .in_8(and_selective_3_out_30), .in_10(and_selective_3_out_31),
    .in_12(and_selective_3_out_32), .in_14(and_selective_3_out_33), .O7(or008_1_o7), .O6(or008_1_o6),
    .O5(or008_1_o5), .O4(or008_1_o4), .O3(or008_1_o3), .O2(or008_1_o2), .O1(or008_1_o1), .O0(or008_1_o0),
    .in_3(and_selective_3_out_18), .in_5(and_selective_3_out_19), .in_7(and_selective_3_out_20),
    .in_9(and_selective_3_out_21), .in_11(and_selective_3_out_22), .in_13(and_selective_3_out_23),
    .in_15(and_selective_3_out_24), .in_16(and_selective_3_out_25));
  AND008 and008_2 (
    .in_1(and_selective_4_out_26), .in_2(and_selective_4_out_27), .in_4(and_selective_4_out_28),
    .in_6(and_selective_4_out_29), .in_8(and_selective_4_out_30), .in_10(and_selective_4_out_31),
    .in_12(and_selective_4_out_32), .in_14(and_selective_4_out_33), .out_17(and008_2_out_17),
    .out_18(and008_2_out_18), .out_19(and008_2_out_19), .out_20(and008_2_out_20), .out_21(and008_2_out_21),
    .out_22(and008_2_out_22), .out_23(and008_2_out_23), .out_24(and008_2_out_24),
    .in_3(and_selective_4_out_18), .in_5(and_selective_4_out_19), .in_7(and_selective_4_out_20),
    .in_9(and_selective_4_out_21), .in_11(and_selective_4_out_22), .in_13(and_selective_4_out_23),
    .in_15(and_selective_4_out_24), .in_16(and_selective_4_out_25));
  AND__7bit and__7bit_1 (
    .in_1(and008_1_out_24), .in_2(or008_1_o0), .in_3(and008_2_out_24), .in_4(not008_1_out_17),
    .in_5(shl_1_out_18), .in_6(shr_1_out_18), .in_7(add008_1_s0), .out_8(out_58));
  AND__7bit and__7bit_2 (
    .in_1(and008_1_out_23), .in_2(or008_1_o1), .in_3(and008_2_out_23), .in_4(not008_1_out_16),
    .in_5(shl_1_s0), .in_6(shr_1_s0), .in_7(add008_1_s1), .out_8(out_56));
  AND__7bit and__7bit_3 (
    .in_1(add008_1_s2), .in_2(or008_1_o2), .in_3(and008_2_out_22), .in_4(not008_1_out_15),
    .in_5(shl_1_out_16), .in_6(shr_1_out_16), .in_7(and008_1_out_22), .out_8(out_55));
  AND__7bit and__7bit_4 (
    .in_1(add008_1_s3), .in_2(and008_1_out_21), .in_3(or008_1_o3), .in_4(and008_2_out_21),
    .in_5(not008_1_out_14), .in_6(shl_1_out_15), .in_7(shr_1_out_15), .out_8(out_54));
  AND__7bit and__7bit_5 (
    .in_1(add008_1_s4), .in_2(or008_1_o4), .in_3(and008_2_out_20), .in_4(not008_1_out_13),
    .in_5(shl_1_out_14), .in_6(shr_1_out_14), .in_7(and008_1_out_20), .out_8(out_53));
  AND__7bit and__7bit_6 (
    .in_1(add008_1_s5), .in_2(and008_1_out_19), .in_3(or008_1_o5), .in_4(and008_2_out_19),
    .in_5(not008_1_out_12), .in_6(shl_1_out_13), .in_7(shr_1_out_13), .out_8(out_52));
  AND__7bit and__7bit_7 (
    .in_1(add008_1_s6), .in_2(and008_1_out_18), .in_3(or008_1_o6), .in_4(and008_2_out_18),
    .in_5(not008_1_out_11), .in_6(shl_1_out_12), .in_7(shr_1_out_12), .out_8(out_51));
  AND__7bit and__7bit_8 (
    .in_1(and008_1_out_17), .in_2(add008_1_s7), .in_3(or008_1_o7), .in_4(and008_2_out_17),
    .in_5(not008_1_out_10), .in_6(shl_1_s7), .in_7(shr_1_s7), .out_8(out_50));
  Zero zero_1 (
    .in_1(out_50), .in_2(out_51), .in_3(out_52), .in_4(out_53), .in_5(out_54), .in_6(out_55), .in_7(out_56),
    .in_8(out_58), .out_9(zero_1_out_9));
  OverFlow overflow_1 (.A(mul_pc_3_out_25), .B(mux_rs_1_out_35), .S(out_50), .out_4(overflow_1_out_4));
  or or_1 (or_1_out, add008_1_c, shr_1_c, shl_1_c);
  Flip_Flop_D_4bit flip_flop_d_4bit_1 (
    .H(and_2bit_1_out_3), .S(1'b1), .R(1'b0), .in_1(overflow_1_out_4), .in_2(out_50), .in_3(zero_1_out_9),
    .in_4(or_1_out), .out_8(V), .out_9(N), .out_10(Z), .out_11(C));

  // Notes on the sheet:
  //   H
  //   S
  //   R
  //   JUMP_SIGNAL
  //   PC_SELECTION
  //   PC_REGISTER
  //   PC+1
  //   SEL_RD
  //   JUMP_ADDS
  //   SEL_RS
  //   OPCODE
  //   CU
  //   IR_REGISTRE
  //   CLOCK
  //   H
  //   S
  //   R
  //   D0
  //   D1
  //   D2
  //   D3
  //   MUX_RD
  //   ENTREE_A_ALU
  //   OPERATION_LOGIQUE
  //   MUX_RS
  //   MUX_RS_D_OR_IMM
  //   ENTREE_B_ALU
  //   SHL
  //   SHR
  //   ADD
  //   ADD
  //   OR
  //   XOR
endmodule

module AND__7bit (
  input  in_1,
  input  in_2,
  input  in_3,
  input  in_4,
  input  in_5,
  input  in_6,
  input  in_7,
  output out_8
);

  wire or_1_out;

  or or_1 (or_1_out, in_1, in_2, in_3, in_4, in_5);
  or or_2 (out_8, or_1_out, in_6, in_7);
endmodule

module MUX_CU (
  input  in_1,
  input  in_2,
  input  in_3,
  input  in_4,
  output out_5,
  output out_6
);

  or or_1 (out_5, in_2, in_4);
  or or_2 (out_6, in_4, in_3);
endmodule

module MUX_WE (
  input  _1,
  input  _0,
  input  WE_D,
  output out_4,
  output out_5,
  output out_6,
  output out_7
);

  wire and_2bit_1_out_3, and_2bit_2_out_3, and_2bit_3_out_3, and_2bit_4_out_3, not_1_out, not_2_out;

  not not_1 (not_1_out, _0);
  not not_2 (not_2_out, _1);
  AND_2bit and_2bit_1 (.in_1(not_1_out), .in_2(not_2_out), .out_3(and_2bit_1_out_3));
  AND_2bit and_2bit_2 (.in_1(_0), .in_2(not_2_out), .out_3(and_2bit_2_out_3));
  AND_2bit and_2bit_3 (.in_1(not_1_out), .in_2(_1), .out_3(and_2bit_3_out_3));
  AND_2bit and_2bit_4 (.in_1(_0), .in_2(_1), .out_3(and_2bit_4_out_3));
  AND_2bit and_2bit_5 (.in_1(WE_D), .in_2(and_2bit_1_out_3), .out_3(out_7));
  AND_2bit and_2bit_6 (.in_1(and_2bit_2_out_3), .in_2(WE_D), .out_3(out_6));
  AND_2bit and_2bit_7 (.in_1(and_2bit_3_out_3), .in_2(WE_D), .out_3(out_5));
  AND_2bit and_2bit_8 (.in_1(and_2bit_4_out_3), .in_2(WE_D), .out_3(out_4));
endmodule

module MUX_SEL_RD (
  input  ALU,
  input  in_2,
  input  MOVE,
  input  in_4,
  input  in_5,
  input  in_6,
  input  in_7,
  input  in_8,
  output out_9,
  output out_10
);

  wire and_1_out, and_2bit_1_out_3, and_2bit_2_out_3, and_2bit_3_out_3, and_2bit_4_out_3, not_1_out,
       not_2_out, not_3_out, not_4_out, not_5_out;

  not not_1 (not_1_out, in_5);
  not not_2 (not_2_out, in_6);
  not not_3 (not_3_out, in_7);
  not not_4 (not_4_out, in_8);
  and and_1 (and_1_out, not_1_out, not_2_out, not_3_out, not_4_out);
  not not_5 (not_5_out, and_1_out);
  AND_2bit and_2bit_1 (.in_1(ALU), .in_2(not_5_out), .out_3(and_2bit_1_out_3));
  AND_2bit and_2bit_2 (.in_1(in_2), .in_2(not_5_out), .out_3(and_2bit_2_out_3));
  AND_2bit and_2bit_3 (.in_1(MOVE), .in_2(and_1_out), .out_3(and_2bit_3_out_3));
  OR_2Bit or_2bit_1 (.in_1(and_2bit_1_out_3), .in_2(and_2bit_3_out_3), .out_3(out_9));
  AND_2bit and_2bit_4 (.in_1(in_4), .in_2(and_1_out), .out_3(and_2bit_4_out_3));
  OR_2Bit or_2bit_2 (.in_1(and_2bit_2_out_3), .in_2(and_2bit_4_out_3), .out_3(out_10));
endmodule

module MUX_MODE (
  input  in_1,
  input  in_2,
  input  in_3,
  input  in_4,
  input  in_5,
  input  in_6,
  output out_7
);

  wire and_1_out, and_2bit_1_out_3, and_2bit_2_out_3, not_1_out, not_2_out, not_3_out, not_4_out, not_5_out;

  not not_1 (not_1_out, in_3);
  not not_2 (not_2_out, in_4);
  not not_3 (not_3_out, in_5);
  not not_4 (not_4_out, in_6);
  and and_1 (and_1_out, not_1_out, not_2_out, not_3_out, not_4_out);
  not not_5 (not_5_out, and_1_out);
  AND_2bit and_2bit_1 (.in_1(in_1), .in_2(not_5_out), .out_3(and_2bit_1_out_3));
  AND_2bit and_2bit_2 (.in_1(in_2), .in_2(and_1_out), .out_3(and_2bit_2_out_3));
  or or_1 (out_7, and_2bit_1_out_3, and_2bit_2_out_3);
endmodule

module MUX_MOVE_11 (
  input  in_1,
  input  in_2,
  input  in_3,
  input  in_4,
  input  in_5,
  input  in_6,
  input  in_7,
  input  in_8,
  input  in_9,
  output out_10,
  output out_11,
  output out_12,
  output out_13,
  output out_14,
  output out_15,
  output out_16,
  output out_17,
  output out_18,
  output out_19,
  output out_20,
  output out_21,
  output out_22,
  output out_23,
  output out_24,
  output out_25
);

  AND_2bit and_2bit_1 (.in_1(in_9), .in_2(in_1), .out_3(out_18));
  AND_2bit and_2bit_2 (.in_1(in_9), .in_2(in_3), .out_3(out_20));
  AND_2bit and_2bit_3 (.in_1(in_9), .in_2(in_2), .out_3(out_19));
  AND_2bit and_2bit_4 (.in_1(in_9), .in_2(in_4), .out_3(out_21));
  AND_2bit and_2bit_5 (.in_1(in_9), .in_2(in_7), .out_3(out_24));
  AND_2bit and_2bit_6 (.in_1(in_6), .in_2(in_9), .out_3(out_23));
  AND_2bit and_2bit_7 (.in_1(in_9), .in_2(in_5), .out_3(out_22));
  AND_2bit and_2bit_8 (.in_1(in_9), .in_2(in_8), .out_3(out_25));

  assign out_10 = 1'b0;
  assign out_11 = 1'b0;
  assign out_12 = 1'b0;
  assign out_13 = 1'b0;
  assign out_14 = 1'b0;
  assign out_15 = 1'b0;
  assign out_16 = 1'b0;
  assign out_17 = 1'b0;
endmodule
